// Logisim project first.circ as structural Verilog: 2 circuits, main circuit main
module main (
  input  in_1,
  input  in_2,
  input  in_3,
  input  in_4,
  input  in_5,
  input  in_6,
  input  in_7,
  input  in_8,
  input  in_9,
  input  in_10,
  input  in_11,
  input  in_12,
  input  in_13,
  input  in_14,
  input  in_15,
  input  in_16,
  input  in_17,
  output out_18,
  output out_19,
  output out_20,
  output out_21,
  output out_22,
  output out_23,
  output out_24,
  output out_25,
  output out_26
);

  wire sum3_1_cout, sum3_2_cout, sum3_3_cout, sum3_4_cout, sum3_5_cout, sum3_6_cout, sum3_7_cout;

  sum3 sum3_1 (.x1(in_14), .x2(in_6), .x3(sum3_2_cout), .sum(out_18), .cout(sum3_1_cout));
  sum3 sum3_2 (.x1(in_15), .x2(in_7), .x3(sum3_3_cout), .sum(out_19), .cout(sum3_2_cout));
  sum3 sum3_3 (.x1(in_16), .x2(in_8), .x3(sum3_4_cout), .sum(out_20), .cout(sum3_3_cout));
  sum3 sum3_4 (.x1(in_9), .x2(in_17), .x3(in_1), .sum(out_21), .cout(sum3_4_cout));
  sum3 sum3_5 (.x1(in_13), .x2(in_5), .x3(sum3_1_cout), .sum(out_26), .cout(sum3_5_cout));
  sum3 sum3_6 (.x1(in_12), .x2(in_4), .x3(sum3_5_cout), .sum(out_25), .cout(sum3_6_cout));
  sum3 sum3_7 (.x1(in_11), .x2(in_3), .x3(sum3_6_cout), .sum(out_24), .cout(sum3_7_cout));
  sum3 sum3_8 (.x1(in_10), .x2(in_2), .x3(sum3_7_cout), .sum(out_23), .cout(out_22));
endmodule

module sum3 (
  input  x1,
  input  x2,
  input  x3,
  output sum,
  output cout
);

  wire and_1_out, and_2_out, and_3_out, and_4_out, and_5_out, and_6_out, and_7_out, not_1_out, not_2_out,
       not_3_out;

  not not_1 (not_1_out, x1);
  not not_2 (not_2_out, x2);
  not not_3 (not_3_out, x3);
  and and_1 (and_1_out, not_1_out, not_2_out, x3);
  and and_2 (and_2_out, not_1_out, x2, not_3_out);
  and and_3 (and_3_out, x1, not_2_out, not_3_out);
  and and_4 (and_4_out, x1, x2, x3);
  and and_5 (and_5_out, x2, x3);
  and and_6 (and_6_out, x1, x3);
  and and_7 (and_7_out, x1, x2);
  or or_1 (sum, and_1_out, and_2_out, and_3_out, and_4_out);
  or or_2 (cout, and_5_out, and_6_out, and_7_out);
endmodule
