// Logisim project third.circ as structural Verilog: 1 circuit, main circuit main
module main (
  output out_1,
  output out_2,
  output out_3,
  output out_4,
  output out_5,
  output out_6
);

  wire and_1_out, clock_1_out, clock_2_out, nand_1_out, nand_2_out, nand_3_out, nand_4_out, not_1_out,
       not_2_out;

  T_Flip_Flop t_ff_1 (.T(and_1_out), .clk(clock_1_out), .Q(out_1));  // open: Qn, reset, preset
  Clock clock_1 (.out(clock_1_out));
  and and_1 (and_1_out, not_1_out, not_2_out);
  not not_1 (not_1_out, out_3);
  not not_2 (not_2_out, out_2);
  T_Flip_Flop t_ff_2 (.T(not_1_out), .clk(clock_1_out), .Q(out_2));  // open: Qn, reset, preset
  T_Flip_Flop t_ff_3 (.T(1'b1), .clk(clock_1_out), .Q(out_3));  // open: Qn, reset, preset
  nand nand_1 (nand_1_out, 1'b1, nand_2_out);
  nand nand_2 (nand_2_out, nand_3_out, nand_4_out);
  T_Flip_Flop t_ff_4 (.T(nand_1_out), .clk(clock_2_out), .Q(out_4));  // open: Qn, reset, preset
  Clock clock_2 (.out(clock_2_out));
  T_Flip_Flop t_ff_5 (.T(nand_3_out), .clk(clock_2_out), .Q(out_5));  // open: Qn, reset, preset
  nand nand_3 (nand_3_out, 1'b1, out_6);
  nand nand_4 (nand_4_out, out_5, 1'b1);
  T_Flip_Flop t_ff_6 (.T(1'b1), .clk(clock_2_out), .Q(out_6));  // open: Qn, reset, preset
endmodule
